# Fritzing sketch Motor Test Sketch (saved by Fritzing 0.9.3b)
circuit board: 18.5cm x 9.27648cm
breadboards: 1

parts:
  U3 = atmega328 [package=dip]
  R17 = Resistor [tolerance=±5% resistance=10k package=THT]
  J58 = rounded female pin header, 3 pins [form="♀ (female rounded)"]
  XTAL = Crystal [frequency="16 Mhz" package=THT]
  R2 = Resistor [tolerance=±5% resistance=100k package=THT]
  R15 = Resistor [tolerance=±5% resistance=1k package=THT]
  Q2 = NPN-Transistor [package="TO92 [THT]"]
  C6 = Ceramic Capacitor [capacitance=22pF package="100 mil [THT, multilayer]"]
  C5 = Ceramic Capacitor [capacitance=22pF package="100 mil [THT, multilayer]"]
  - = screw terminal, 2 pins
  C7 = Ceramic Capacitor [capacitance="100 nF" package="100 mil [THT, multilayer]"]
  C10 = Electrolytic Capacitor [capacitance=33µF voltage=25V package="100 mil [THT, electrolytic]"]
  C11 = Electrolytic Capacitor [capacitance=33µF voltage=25V package="100 mil [THT, electrolytic]"]
  R13 = Resistor [tolerance=±5% resistance=1k package=THT]
  R14 = Resistor [tolerance=±5% resistance=1k package=THT]
  R16 = Resistor [tolerance=±5% resistance=1k package=THT]
  C9 = Ceramic Capacitor [capacitance="100 nF" package="100 mil [THT, multilayer]"]
  C8 = Ceramic Capacitor [capacitance="100 nF" package="100 mil [THT, multilayer]"]
  Q10 = MOSFET-NCHANNEL [package=sot23-3]
  R12 = Resistor [tolerance=±5% resistance=1k package=THT]
  R_Y = screw terminal, 2 pins
  C2 = Capacitor Polarized [package=cpol-radial-1000uf-25v]
  R11 = Resistor [tolerance=±5% resistance=1k package=THT]
  R22 = Resistor [tolerance=±5% resistance=56k package=THT]
  R23 = Resistor [tolerance=±5% resistance=56k package=THT]
  R25 = Resistor [tolerance=±5% resistance=56k package=THT]
  R27 = Resistor [tolerance=±5% resistance=56k package=THT]
  R29 = Resistor [tolerance=±5% resistance=56k package=THT]
  R24 = Resistor [tolerance=±5% resistance=56k package=THT]
  R26 = Resistor [tolerance=±5% resistance=22k package=THT]
  R28 = Resistor [tolerance=±5% resistance=22k package=THT]
  M1 = V18ZA2P [package=v18za2p]
  M2 = V18ZA2P [package=v18za2p]
  D6 = Diode [package=diode-1n4001]
  D7 = Diode [package=diode-1n4001]
  SIM800L_20MM1 = SIM800L_20MM
  B_Y_R = screw terminal, 3 pins
  Q7 = Sharp PC817 [package=THT]
  Q8 = Sharp PC817 [package=THT]
  Q9 = Sharp PC817 [package=THT]
  J48 = rounded female pin header, 2 pins [form="♀ (female rounded)"]
  RESET1 = Pushbutton [package="[THT]"]
  ON/OFF = SWITCH-DPDT [package=os]
  J60 = Rectifier_6A [package=THT]
  J69 = 3pth XH JST Custom [form="♀ (female rounded)" package=THT]
  J72 = 4pth XH JST CUSTOM [form="♀ (female rounded)" package=THT]
  J73 = 4pth XH JST CUSTOM [form="♀ (female rounded)" package=THT]
  J77 = 2PTH JST FROM HEADER 5 [form="♀ (female rounded)" package=THT]
  C12 = Electrolytic Capacitor [capacitance=0.47mF voltage=10V package="200 mil [THT, electrolytic]"]
  D8 = Diode [package=diode-1n4001]
  TP4056_Battery_Charge_Module1 = TP4056 Lithium Ion Battery Charger
  Step_Down_Module1 = MP1584 Step Down Module [part_number=MP1584]
  LM2596_Module1 = LM2596 Step Down Module
  D9 = Diode [package=diode-1n4001]
  R30 = Resistor [tolerance=±5% resistance=100k package=THT]

nets:
  N1: U3.RESET, R17.Pin_1, RESET1.Pin_1, RESET1.Pin_2
  N2: U3.D0_(RX), J48.pin1
  N3: U3.D1_(TX), J48.pin2
  N4: U3.D2, R16.Pin_0
  N5: U3.D3_(PWM), R15.Pin_1
  N6: U3.VCC, U3.AVCC, U3.AREF, C7.1, C9.0, C8.1, Q10.S, SIM800L_20MM1.PIN2, C12.+, D9.C
  N7: U3.GND, Q2.E, C6.0, C5.1, C7.0, C10.-, C11.-, C9.1, C8.0, SIM800L_20MM1.PIN_6, Q7.Pin_3, Q8.Pin_3, Q9.Pin_3, RESET1.Pin_3, RESET1.Pin_4, C12.-, Step_Down_Module1.OUT-
  N8: U3.XLAT1, XTAL.pin_0, C5.0
  N9: U3.XLAT2, XTAL.pin_1, C6.1
  N10: U3.D5_(PWM), J58.pin1
  N11: U3.D6_(PWM), J58.pin2
  N12: U3.D7, J58.pin3
  N13: U3.D9_(PWM), R30.Pin_0
  N14: R2.Pin_0, TP4056_Battery_Charge_Module1.IN-, Step_Down_Module1.IN-, LM2596_Module1.OUT-
  N15: R2.Pin_1, Q10.G, TP4056_Battery_Charge_Module1.IN+, Step_Down_Module1.IN+, LM2596_Module1.OUT+
  N16: R15.Pin_0, Q2.B
  N17: Q2.C, SIM800L_20MM1.PIN_8
  N18: -.pin1, C2.-, J60.DC_-, TP4056_Battery_Charge_Module1.B-, TP4056_Battery_Charge_Module1.OUT-, LM2596_Module1.IN-
  N19: -.pin2, TP4056_Battery_Charge_Module1.B+
  N20: C10.+, R14.Pin_1, Q7.Pin_4
  N21: C11.+, R13.Pin_1, Q8.Pin_4
  N22: R16.Pin_1, SIM800L_20MM1.PIN_7
  N23: Q10.D, TP4056_Battery_Charge_Module1.OUT+
  N24: R12.Pin_0, Q9.Pin_4
  N25: R_Y.pin1, J69.pin3
  N26: R_Y.pin2, J69.pin1
  N27: C2.+, J60.DC_+, D8.A
  N28: R11.Pin_0, Q9.Pin_1
  N29: R22.Pin_0, R25.Pin_0, B_Y_R.pin1
  N30: R22.Pin_1, M1.P$2, D6.C
  N31: R23.Pin_0, B_Y_R.pin2
  N32: R23.Pin_1, R27.Pin_0, M1.P$1
  N33: R25.Pin_1, R29.Pin_0, M2.P$1
  N34: R27.Pin_1, J72.pin3
  N35: R29.Pin_1, J72.pin1
  N36: R24.Pin_0, B_Y_R.pin3
  N37: R24.Pin_1, M2.P$2, D7.C
  N38: R26.Pin_0, J72.pin4
  N39: R26.Pin_1, D6.A
  N40: R28.Pin_0, J72.pin2
  N41: R28.Pin_1, D7.A
  N42: Q7.Pin_1, J73.pin3
  N43: Q7.Pin_2, J73.pin4
  N44: Q8.Pin_1, J73.pin1
  N45: Q8.Pin_2, J73.pin2
  N46: ON/OFF.2, ON/OFF.5
  N47: ON/OFF.3, ON/OFF.6
  N48: J60.AC_IN#1, J77.pin2
  N49: J60.AC_IN#2, J77.pin1
  N50: D8.C, LM2596_Module1.IN+
  N51: Step_Down_Module1.OUT+, D9.A, R30.Pin_1

notes:
  M-
  RX
  TX
  STX
  SRX
  1
  C
  MOTOR
  FeedBack
  +
  Battery
  J1

custom parts:
  Rectifier_6A: stand Up rectifier 6A
  3pth XH JST Custom: 3PTH XH JST
  2PTH JST FROM HEADER 5: Generic rounded female header
  TP4056 Lithium Ion Battery Charger: A lithium battery charging and powering shield.
  MP1584 Step Down Module: Step Down Module based on MP1584
  LM2596 Step Down Module: LM2596 Step Down Regulator
